// Digital circuit 4bit_Processor.dig as structural Verilog
module _4bit_Processor (
  input  Clk,
  input  PCLoad,
  input  [3:0] PCDataIn,
  input  [3:0] RamDataIn,
  input  RamReadEnable,
  input  RamWriteEnable,
  input  CUEnable,
  output [3:0] Opcode,
  output [3:0] ALUOut,
  output [2:0] ALUCtrl,
  output [3:0] Address,
  output [3:0] RR1,
  output [3:0] RR2,
  output ZeroFlag
);

  wire cu_1_il, cu_1_pcinc, cu_1_rr1, cu_1_rr2, cu_1_we, cu_1_wreg;
  wire [0:0] cu_1_if;
  wire [3:0] multiplexer_1_out, RAM_out;

  RAM RAM (.Address(Address), .Data(RamDataIn), .Clk(Clk), .Read(RamReadEnable), .Write(RamWriteEnable), .Out(RAM_out));
  gp_register IR (.Ctrl({1'b0, cu_1_if[0]}), .In(RAM_out), .Clk(Clk), .Q(Opcode));  // open: Qinv
  PC PC (.Inc(cu_1_pcinc), .Load(PCLoad), .In(PCDataIn), .Clk(Clk), .Out(Address));
  CU cu_1 (
    .Opcode(Opcode), .Clk(Clk), .Enable(CUEnable), .RR1(cu_1_rr1), .RR2(cu_1_rr2), .WReg(cu_1_wreg),
    .WE(cu_1_we), .IL(cu_1_il), .ALU(ALUCtrl), .PCInc(cu_1_pcinc), .IF(cu_1_if[0]));
  Multiplexer #(.Bits(4)) multiplexer_1 (.sel(cu_1_il), .in_0(ALUOut), .in_1(RAM_out), .out(multiplexer_1_out));
  RegisterFile registerfile_1 (
    .RR1(cu_1_rr1), .RR2(cu_1_rr2), .WR(cu_1_wreg), .WD(multiplexer_1_out), .WE(cu_1_we), .Clk(Clk),
    .RD1(RR1), .RD2(RR2));
  ALU alu_1 (.A(RR1), .B(RR2), .Control(ALUCtrl), .Output(ALUOut), .Zero(ZeroFlag));
endmodule
