// Digital circuit 4bit_subtractor.dig as structural Verilog
module _4bit_subtractor (
  input  [3:0] A,
  input  [3:0] B,
  input  Control,
  output [3:0] Output
);

  wire [3:0] _4bit_full_adder_1_sum, multiplexer_1_out, not_1_out;

  assign not_1_out = ~B;  // Not not_1, 4 bits wide
  _4bit_full_adder _4bit_full_adder_1 (.A(4'b0001), .B(not_1_out), .Sum(_4bit_full_adder_1_sum));
  Multiplexer #(.Bits(4)) multiplexer_1 (
    .sel(Control), .in_0(_4bit_full_adder_1_sum), .in_1(B), .out(multiplexer_1_out));
  _4bit_full_adder _4bit_full_adder_2 (.A(A), .B(multiplexer_1_out), .Sum(Output));
endmodule
