// Digital circuit ALU.dig as structural Verilog
module ALU (
  input  [3:0] A,
  input  [3:0] B,
  input  [2:0] Control,
  output [3:0] Output,
  output Zero
);

  wire [3:0] _4bit_full_adder_1_sum, _4bit_subtractor_1_output, and_1_out, or_1_out, slt_1_out, xor_1_out;

  _4bit_full_adder _4bit_full_adder_1 (.A(A), .B(B), .Sum(_4bit_full_adder_1_sum));
  _4bit_subtractor _4bit_subtractor_1 (.A(A), .B(B), .Control(1'b0), .Output(_4bit_subtractor_1_output));
  AND and_1 (.A(A), .B(B), .Out(and_1_out));
  OR or_1 (.A(A), .B(B), .Out(or_1_out));
  SLT slt_1 (.A(A), .B(B), .Out(slt_1_out));
  XOR xor_1 (.A(A), .B(B), .Out(xor_1_out));
  Multiplexer #(.Selector_Bits(3), .Bits(4)) multiplexer_1 (
    .sel(Control), .in_0(_4bit_full_adder_1_sum), .in_1(_4bit_subtractor_1_output), .in_2(and_1_out),
    .in_3(or_1_out), .in_4(xor_1_out), .in_5(slt_1_out), .in_6(A), .in_7(4'b0000), .out(Output));
  nor nor_1 (Zero, Output[0], Output[1], Output[2], Output[3]);
endmodule
