// Digital circuit SLT.dig as structural Verilog
module SLT (
  input  [3:0] A,
  input  [3:0] B,
  output [3:0] Out
);

  wire [2:0] _4bit_subtractor_1_output;

  _4bit_subtractor _4bit_subtractor_1 (.A(A), .B(B), .Control(1'b0), .Output({Out[0], _4bit_subtractor_1_output}));

  assign Out[3:1] = 3'b000;
endmodule
