// Digital circuit PC.dig as structural Verilog
module PC (
  input  Inc,
  input  Load,
  input  [3:0] In,
  input  Clk,
  output [3:0] Out
);

  wire [3:0] _4bit_full_adder_1_sum, multiplexer_1_out;

  _4bit_register _4bit_register_1 (.D(_4bit_full_adder_1_sum), .Clk(Clk), .Q(Out));  // open: Qinv
  Multiplexer #(.Bits(4)) multiplexer_1 (.sel(Load), .in_0(Out), .in_1(In), .out(multiplexer_1_out));
  _4bit_full_adder _4bit_full_adder_1 (.A(multiplexer_1_out), .B({3'b000, Inc}), .Sum(_4bit_full_adder_1_sum));
endmodule
