// Digital circuit RAM.dig as structural Verilog
module RAM (
  input  [3:0] Address,
  input  [3:0] Data,
  input  Clk,
  input  Read,
  input  Write,
  output [3:0] Out
);

  wire and_1_out, and_3_out, xor_1_out;
  wire [0:0] and_2_out;
  wire [1:0] demultiplexer_1_out_0, demultiplexer_1_out_1, demultiplexer_1_out_2, demultiplexer_1_out_3,
       demultiplexer_1_out_4, demultiplexer_1_out_5, demultiplexer_1_out_6, demultiplexer_1_out_7,
       demultiplexer_1_out_8, demultiplexer_1_out_9, demultiplexer_1_out_10, demultiplexer_1_out_11,
       demultiplexer_1_out_12, demultiplexer_1_out_13, demultiplexer_1_out_14, demultiplexer_1_out_15;
  wire [3:0] _0_q, _1_q, _2_q, _3_q, _4_q, _5_q, _6_q, _7_q, _8_q, _9_q, _10_q, _11_q, _12_q, _13_q, _14_q,
       _15_q, multiplexer_1_out;

  xor xor_1 (xor_1_out, Read, Write);
  and and_1 (and_1_out, Read, xor_1_out);
  and and_2 (and_2_out[0], xor_1_out, Write);
  and and_3 (and_3_out, Clk, and_2_out[0]);
  Demultiplexer #(.Selector_Bits(4), .Bits(2)) demultiplexer_1 (
    .sel(Address), .in({1'b0, and_2_out[0]}), .out_0(demultiplexer_1_out_0), .out_1(demultiplexer_1_out_1),
    .out_2(demultiplexer_1_out_2), .out_3(demultiplexer_1_out_3), .out_4(demultiplexer_1_out_4),
    .out_5(demultiplexer_1_out_5), .out_6(demultiplexer_1_out_6), .out_7(demultiplexer_1_out_7),
    .out_8(demultiplexer_1_out_8), .out_9(demultiplexer_1_out_9), .out_10(demultiplexer_1_out_10),
    .out_11(demultiplexer_1_out_11), .out_12(demultiplexer_1_out_12), .out_13(demultiplexer_1_out_13),
    .out_14(demultiplexer_1_out_14), .out_15(demultiplexer_1_out_15));
  gp_register _0 (.Ctrl(demultiplexer_1_out_15), .In(Data), .Clk(and_3_out), .Q(_0_q));  // open: Qinv
  gp_register _1 (.Ctrl(demultiplexer_1_out_14), .In(Data), .Clk(and_3_out), .Q(_1_q));  // open: Qinv
  gp_register _2 (.Ctrl(demultiplexer_1_out_13), .In(Data), .Clk(and_3_out), .Q(_2_q));  // open: Qinv
  gp_register _3 (.Ctrl(demultiplexer_1_out_12), .In(Data), .Clk(and_3_out), .Q(_3_q));  // open: Qinv
  gp_register _4 (.Ctrl(demultiplexer_1_out_11), .In(Data), .Clk(and_3_out), .Q(_4_q));  // open: Qinv
  gp_register _5 (.Ctrl(demultiplexer_1_out_10), .In(Data), .Clk(and_3_out), .Q(_5_q));  // open: Qinv
  gp_register _6 (.Ctrl(demultiplexer_1_out_9), .In(Data), .Clk(and_3_out), .Q(_6_q));  // open: Qinv
  gp_register _7 (.Ctrl(demultiplexer_1_out_8), .In(Data), .Clk(and_3_out), .Q(_7_q));  // open: Qinv
  assign Out = and_1_out ? multiplexer_1_out : 4'bz;  // Driver driver_1
  gp_register _8 (.Ctrl(demultiplexer_1_out_7), .In(Data), .Clk(and_3_out), .Q(_8_q));  // open: Qinv
  gp_register _9 (.Ctrl(demultiplexer_1_out_6), .In(Data), .Clk(and_3_out), .Q(_9_q));  // open: Qinv
  gp_register _10 (.Ctrl(demultiplexer_1_out_5), .In(Data), .Clk(and_3_out), .Q(_10_q));  // open: Qinv
  gp_register _11 (.Ctrl(demultiplexer_1_out_4), .In(Data), .Clk(and_3_out), .Q(_11_q));  // open: Qinv
  Multiplexer #(.Selector_Bits(4), .Bits(4)) multiplexer_1 (
    .sel(Address), .in_0(_15_q), .in_1(_14_q), .in_2(_13_q), .in_3(_12_q), .in_4(_11_q), .in_5(_10_q),
    .in_6(_9_q), .in_7(_8_q), .in_8(_7_q), .in_9(_6_q), .in_10(_5_q), .in_11(_4_q), .in_12(_3_q),
    .in_13(_2_q), .in_14(_1_q), .in_15(_0_q), .out(multiplexer_1_out));
  gp_register _12 (.Ctrl(demultiplexer_1_out_3), .In(Data), .Clk(and_3_out), .Q(_12_q));  // open: Qinv
  gp_register _13 (.Ctrl(demultiplexer_1_out_2), .In(Data), .Clk(and_3_out), .Q(_13_q));  // open: Qinv
  gp_register _14 (.Ctrl(demultiplexer_1_out_1), .In(Data), .Clk(and_3_out), .Q(_14_q));  // open: Qinv
  gp_register _15 (.Ctrl(demultiplexer_1_out_0), .In(Data), .Clk(and_3_out), .Q(_15_q));  // open: Qinv
endmodule
