// Digital circuit RegisterFile.dig as structural Verilog
module RegisterFile (
  input  RR1,
  input  RR2,
  input  WR,
  input  [3:0] WD,
  input  WE,
  input  Clk,
  output [3:0] RD1,
  output [3:0] RD2
);

  wire [0:0] demultiplexer_1_out_0, demultiplexer_1_out_1;
  wire [3:0] A_q, B_q;

  Demultiplexer demultiplexer_1 (.sel(WR), .in(WE), .out_0(demultiplexer_1_out_0[0]), .out_1(demultiplexer_1_out_1[0]));
  gp_register A (.Ctrl({1'b0, demultiplexer_1_out_0[0]}), .In(WD), .Clk(Clk), .Q(A_q));  // open: Qinv
  gp_register B (.Ctrl({1'b0, demultiplexer_1_out_1[0]}), .In(WD), .Clk(Clk), .Q(B_q));  // open: Qinv
  Multiplexer #(.Bits(4)) multiplexer_1 (.sel(RR1), .in_0(A_q), .in_1(B_q), .out(RD1));
  Multiplexer #(.Bits(4)) multiplexer_2 (.sel(RR2), .in_0(A_q), .in_1(B_q), .out(RD2));
endmodule
