// Digital circuit gp_register.dig as structural Verilog
module gp_register (
  input  [1:0] Ctrl,
  input  [3:0] In,
  input  Clk,
  output [3:0] Q,
  output [3:0] Qinv
);

  wire [3:0] multiplexer_1_out;

  _4bit_register _4bit_register_1 (.D(multiplexer_1_out), .Clk(Clk), .Q(Q), .Qinv(Qinv));
  Multiplexer #(.Selector_Bits(2), .Bits(4)) multiplexer_1 (
    .sel(Ctrl), .in_0(Q), .in_1(In), .in_2(4'b0000), .in_3(4'b0000), .out(multiplexer_1_out));
endmodule
